// Logisim project control.circ as structural Verilog: 1 circuit, main circuit main
module main (
  input  [5:0] instruction_31_26,
  output RegDst,
  output Jump,
  output Branch,
  output MemRead,
  output MemtoReg,
  output [3:0] ALUOp,
  output MemWrite,
  output ALUSrc,
  output RegWrite
);


  assign ALUSrc = 1'b1;
  assign Branch = 1'b1;
  assign RegWrite = 1'b1;
endmodule
